// Logisim project ALU.circ as structural Verilog: 2 circuits, main circuit main
module ALU (
  input  [31:0] Op1,
  input  [31:0] op2,
  input  Sub,
  input  [2:0] Opcode,
  output [31:0] Res,
  output C,
  output Z
);

  wire adder_2_cout, decoder_1_out2, decoder_1_out3, isSLT, not_2_out, xor_2_out;
  wire [4:0] bit_extender_2_out, bit_extender_3_out, bit_extender_4_out;
  wire [31:0] ADD, adder_2_out, AND, bit_extender_1_out, not_1_out, OR, shifter_2_out, shifter_3_out, SLL,
       SLT, SLTU, SRL, XOR, xor_1_out;

  Decoder #(.select(3), .enable("false")) decoder_1 (
    .out2(decoder_1_out2), .out3(decoder_1_out3), .sel(Opcode));  // open: out0, out1, out4, out5, out6, out7
  or or_1 (isSLT, decoder_1_out2, decoder_1_out3);
  assign xor_1_out = op2 ^ bit_extender_1_out;  // XOR_Gate xor_1, 32 bits wide
  assign bit_extender_1_out = {{31{Sub}}, Sub};  // Bit_Extender bit_extender_1
  assign not_1_out = ~op2;  // NOT_Gate not_1, 32 bits wide
  Adder #(.width(32)) adder_1 (.a(Op1), .b(xor_1_out), .out(ADD), .cin(Sub), .cout(C));
  Adder #(.width(32)) adder_2 (.a(Op1), .b(not_1_out), .out(adder_2_out), .cin(1'b1), .cout(adder_2_cout));
  not not_2 (not_2_out, adder_2_cout);
  xor xor_2 (xor_2_out, op2[31], adder_2_out[31]);
  Bit_Extender #(.in_width(32), .out_width(5)) bit_extender_2 (.in(op2), .out(bit_extender_2_out));
  Bit_Extender #(.in_width(32), .out_width(5)) bit_extender_3 (.in(op2), .out(bit_extender_3_out));
  Bit_Extender #(.in_width(32), .out_width(5)) bit_extender_4 (.in(op2), .out(bit_extender_4_out));
  assign SLT = {{31{1'b0}}, xor_2_out};  // Bit_Extender bit_extender_5
  assign SLTU = {{31{1'b0}}, not_2_out};  // Bit_Extender bit_extender_6
  Shifter #(.width(32)) shifter_1 (.in(Op1), .\dist (bit_extender_2_out), .out(SLL));
  assign XOR = Op1 ^ op2;  // XOR_Gate xor_3, 32 bits wide
  Shifter #(.width(32), .shift("lr")) shifter_2 (.in(Op1), .\dist (bit_extender_3_out), .out(shifter_2_out));
  Shifter #(.width(32), .shift("ar")) shifter_3 (.in(Op1), .\dist (bit_extender_4_out), .out(shifter_3_out));
  assign OR = Op1 | op2;  // OR_Gate or_2, 32 bits wide
  assign AND = Op1 & op2;  // AND_Gate and_1, 32 bits wide
  Multiplexer #(.width(32), .enable("false")) multiplexer_1 (
    .in0(shifter_2_out), .in1(shifter_3_out), .out(SRL), .sel(Sub));
  Multiplexer #(.select(3), .width(32), .enable("false")) multiplexer_2 (
    .in0(ADD), .in1(SLL), .in2(SLT), .in3(SLTU), .in4(XOR), .in5(SRL), .in6(OR), .in7(AND), .out(Res),
    .sel(Opcode));
  nor nor_1 (Z, Res[0], Res[1], Res[2], Res[3], Res[4], Res[5], Res[6], Res[7], Res[8], Res[9], Res[10], Res[11], Res[12], Res[13], Res[14], Res[15], Res[17], Res[18], Res[19], Res[20], Res[21], Res[22], Res[23], Res[24], Res[25], Res[26], Res[27], Res[28], Res[29], Res[30], Res[31], Res[16]);

  // Other names for the same wires on the sheet: Cout = C
endmodule

module main (
);

  ALU alu_1 ();  // open: Op1, op2, Sub, Opcode, Res, C, Z
endmodule
