// Logisim project cpu - Copy.circ as structural Verilog: 2 circuits, main circuit datapath
module datapath (
  input  pcsrc,
  input  mdrload,
  input  mem2reg,
  input  pcload,
  input  regwrite,
  input  [2:0] opc,
  input  sub,
  input  IOrD,
  input  ALoad,
  input  alusrc1,
  input  regsrc2,
  input  aluoutload,
  input  IRload,
  input  [4:0] rs1,
  input  [4:0] rs2,
  input  [4:0] rd,
  input  BLoad,
  input  [1:0] alusrc2,
  input  MemWr,
  input  MemRd,
  input  [31:0] imm,
  input  [1:0] width,
  input  Extend,
  input  in_24,
  output z,
  output c,
  output [31:0] Inst
);

  wire cd;
  wire [4:0] multiplexer_4_out;
  wire [31:0] alu_1_res, b, memory_1_data, multiplexer_1_out, multiplexer_2_out, multiplexer_3_out,
       multiplexer_5_out, multiplexer_6_out, regfile_1_r1_d, regfile_1_r2_d, register_1_q, register_2_q,
       register_4_q, register_6_q;

  Multiplexer #(.width(32), .enable("false")) multiplexer_1 (
    .in0(register_6_q), .in1(alu_1_res), .out(multiplexer_1_out), .sel(pcsrc));
  Register #(.width(32)) register_1 (.D(multiplexer_1_out), .en(pcload), .Q(register_1_q), .clk(in_24));  // open: clr
  Multiplexer #(.width(32), .enable("false")) multiplexer_2 (
    .in0(register_1_q), .in1(b), .out(multiplexer_2_out), .sel(IOrD));
  Memory memory_1 (
    .Address(multiplexer_2_out), .Input(b), .Clock(in_24), .Load(MemRd), .Store(MemWr), .Data(memory_1_data),
    .Width(width), .Extend(Extend), .DClock(cd));  // open: Clear
  Register #(.width(32)) register_2 (.D(memory_1_data), .en(mdrload), .Q(register_2_q), .clk(cd));  // open: clr
  Register #(.width(32)) register_3 (.D(memory_1_data), .en(IRload), .Q(Inst), .clk(cd));  // open: clr
  Multiplexer #(.width(32), .enable("false")) multiplexer_3 (
    .in0(register_6_q), .in1(register_2_q), .out(multiplexer_3_out), .sel(mem2reg));
  Multiplexer #(.width(5), .enable("false")) multiplexer_4 (
    .in0(rs2), .in1(rd), .out(multiplexer_4_out), .sel(regsrc2));
  regfile regfile_1 (
    .wr(multiplexer_3_out), .r1_a(rs1), .r1_d(regfile_1_r1_d), .r2_a(multiplexer_4_out),
    .r2_d(regfile_1_r2_d), .w_a(rd), .e_en(regwrite), .clk(in_24));
  Register #(.width(32)) register_4 (.D(regfile_1_r1_d), .en(ALoad), .Q(register_4_q), .clk(in_24));  // open: clr
  Register #(.width(32)) register_5 (.D(regfile_1_r2_d), .en(BLoad), .Q(b), .clk(in_24));  // open: clr
  Multiplexer #(.width(32), .enable("false")) multiplexer_5 (
    .in0(register_1_q), .in1(register_4_q), .out(multiplexer_5_out), .sel(alusrc1));
  ALU alu_1 (.Op1(multiplexer_5_out), .op2(multiplexer_6_out), .Sub(sub), .Opcode(opc), .Res(alu_1_res), .C(c), .Z(z));
  Multiplexer #(.select(2), .width(32), .enable("false")) multiplexer_6 (
    .in0(32'h4), .in1(b), .in2(imm), .out(multiplexer_6_out), .sel(alusrc2));  // open: in3
  Register #(.width(32)) register_6 (.D(alu_1_res), .en(aluoutload), .Q(register_6_q), .clk(in_24));  // open: clr

  // Other names for the same wires on the sheet: clk = in_24
endmodule

module control_unit (
  input  clk,
  input  [31:0] in_2
);

  wire ALU_Out_Ld, ALU_Src1, and_17_out, AUIPC, BRANCH, decoder_1_out0, decoder_1_out1, decoder_1_out3,
       decoder_2_out0, decoder_2_out1, decoder_2_out3, decoder_2_out4, decoder_2_out5, decoder_3_out1,
       decoder_3_out2, decoder_3_out3, decoder_3_out4, halt, I_Or_D, IR_Load, JAL, JALR, LOAD, LUI, MISC_MEM,
       OP, OP_IMM, or_1_out, or_2_out, or_3_out, or_5_out, PC_SRC, STORE, Sub, SYSTEM, valid_opc;
  wire [1:0] ALU_Src2;
  wire [2:0] ALU_Op, counter_1_q;
  wire [19:0] and_13_out, and_14_out, and_15_out, bit_extender_3_out, bit_extender_4_out, bit_extender_5_out,
       imm_i, imm_s_sb, or_4_out;
  wire [31:0] imm;

  Decoder #(.select(2), .disabled(0)) decoder_1 (
    .out0(decoder_1_out0), .out1(decoder_1_out1), .out3(decoder_1_out3), .sel(in_2[6:5]), .en(valid_opc));  // open: out2
  and and_1 (valid_opc, in_2[0], in_2[1]);
  Decoder #(.select(3), .disabled(0)) decoder_2 (
    .out0(decoder_2_out0), .out1(decoder_2_out1), .out3(decoder_2_out3), .out4(decoder_2_out4),
    .out5(decoder_2_out5), .sel(in_2[4:2]), .en(valid_opc));  // open: out2, out6, out7
  and and_2 (LOAD, decoder_1_out0, decoder_2_out0);
  and and_3 (STORE, decoder_1_out1, decoder_2_out0);
  and and_4 (BRANCH, decoder_1_out3, decoder_2_out0);
  and and_5 (MISC_MEM, decoder_1_out0, decoder_2_out3);
  and and_6 (OP_IMM, decoder_1_out0, decoder_2_out4);
  and and_7 (LUI, decoder_1_out1, decoder_2_out5);
  and and_8 (OP, decoder_1_out1, decoder_2_out4);
  and and_9 (JALR, decoder_2_out1, decoder_1_out3);
  and and_10 (JAL, decoder_2_out3, decoder_1_out3);
  and and_11 (AUIPC, decoder_1_out0, decoder_2_out5);
  and and_12 (SYSTEM, decoder_2_out4, decoder_1_out3);
  datapath datapath_1 ();  // open: pcload, in_24, alusrc1, alusrc2, mdrload, mem2reg, regwrite, ALoad, opc, sub, pcsrc, MemWr, IOrD, IRload, Inst, regsrc2, rs1, rs2, rd, BLoad, imm, z, c, MemRd, width, Extend, aluoutload
  nor nor_1 (halt, MISC_MEM, LOAD, OP_IMM, AUIPC, STORE, OP, LUI, BRANCH, JALR, JAL, SYSTEM);
  or or_1 (or_1_out, AUIPC, LUI, JAL);
  or or_2 (or_2_out, STORE, BRANCH);
  or or_3 (or_3_out, LOAD, JALR);
  assign imm_s_sb = {{13{in_2[31]}}, in_2[31:25]};  // Bit_Extender bit_extender_1
  assign imm_i = {{8{in_2[31]}}, in_2[31:20]};  // Bit_Extender bit_extender_2
  assign bit_extender_3_out = {{19{or_1_out}}, or_1_out};  // Bit_Extender bit_extender_3
  assign bit_extender_4_out = {{19{or_2_out}}, or_2_out};  // Bit_Extender bit_extender_4
  assign bit_extender_5_out = {{19{or_3_out}}, or_3_out};  // Bit_Extender bit_extender_5
  assign and_13_out = in_2[31:12] & bit_extender_3_out;  // AND_Gate and_13, 20 bits wide
  assign and_14_out = imm_s_sb & bit_extender_4_out;  // AND_Gate and_14, 20 bits wide
  assign and_15_out = imm_i & bit_extender_5_out;  // AND_Gate and_15, 20 bits wide
  Pull_Resistor pull_resistor_1 (.node(ALU_Src1));
  Pull_Resistor pull_resistor_2 (.node(ALU_Src2));
  Pull_Resistor pull_resistor_3 (.node(IR_Load));
  Pull_Resistor pull_resistor_4 (.node(ALU_Op));
  Pull_Resistor pull_resistor_5 (.node(Sub));
  Pull_Resistor pull_resistor_6 (.node(PC_SRC));
  Pull_Resistor pull_resistor_7 (.node(I_Or_D));
  Pull_Resistor pull_resistor_8 (.node(IR_Load));
  Pull_Resistor pull_resistor_9 (.node(IR_Load));
  Pull_Resistor pull_resistor_10 (.node(imm));
  Pull_Resistor pull_resistor_11 (.node(ALU_Out_Ld));
  assign or_4_out = and_13_out | and_14_out | and_15_out;  // OR_Gate or_4, 20 bits wide
  assign imm = {{12{or_4_out[19]}}, or_4_out};  // Bit_Extender bit_extender_6
  or or_5 (or_5_out, JALR, JAL);
  and and_16 (ALU_Out_Ld, decoder_3_out1, or_5_out);
  and and_17 (and_17_out, decoder_3_out1, JALR);
  Multiplexer #(.width(2), .enable("false")) multiplexer_1 (
    .in1(2'b10), .out(ALU_Src2), .sel(ALU_Out_Ld));  // open: in0
  Counter #(.width(3), .max('h4)) counter_1 (.Q(counter_1_q), .clk(clk));  // open: load, D, count, carry, clr
  Decoder #(.select(3), .enable("false")) decoder_3 (
    .out0(IR_Load), .out1(decoder_3_out1), .out2(decoder_3_out2), .out3(decoder_3_out3),
    .out4(decoder_3_out4), .sel(counter_1_q));  // open: out5, out6, out7
  Decoder #(.enable("false")) decoder_4 ();  // open: out0, out1, sel

  // Other names for the same wires on the sheet: inst[31:0] = in_2; inst_4_2[2:0] = in_2[4:2];
  //   inst_6_5[1:0] = in_2[6:5]; rd[4:0] = in_2[11:7]; funct3[2:0] = in_2[14:12]; imm_u_uj[19:0] = in_2[31:12];
  //   rs1[4:0] = in_2[19:15]; rs2[4:0] = in_2[24:20]; funct7[6:0] = in_2[31:25]; Mem_Read = IR_Load;
  //   PC_Src_t = IR_Load

  // Notes on the sheet:
  //   pc=pc+4
  //   IR <- Mem[PC]
  //   Fetch
  //   UJ/JALR:
  //   (PC)
endmodule
