// Logisim project memory-v1.circ as structural Verilog: 1 circuit, main circuit Memory
module Memory (
  input  [31:0] Address,
  input  Clear,
  input  [31:0] Input,
  input  Load,
  input  Store,
  input  Clock,
  input  Extend,
  input  [1:0] Width,
  output [31:0] Data,
  output DClock
);

  wire and_1_out, and_2_out, and_3_out, and_4_out, and_5_out, and_14_out, and_15_out, and_16_out, not_1_out,
       not_2_out, not_3_out, not_4_out, not_5_out, not_6_out, not_7_out, not_8_out, not_9_out, not_10_out,
       not_11_out, not_12_out, not_13_out, not_14_out, not_15_out, not_16_out, not_17_out, not_18_out,
       not_19_out, not_20_out, not_21_out, not_22_out, not_23_out, not_24_out, not_25_out, not_26_out,
       not_27_out, not_28_out, not_29_out, not_30_out, not_31_out, not_32_out, not_33_out, not_34_out,
       not_35_out, not_36_out, not_37_out, not_38_out, not_39_out, not_40_out, not_41_out, not_42_out,
       not_43_out, not_44_out, not_45_out, not_46_out, not_47_out, not_48_out, not_49_out, not_50_out,
       not_51_out, not_52_out, not_53_out, not_54_out, not_55_out, not_56_out, not_57_out, not_58_out,
       not_59_out, not_60_out, not_61_out, not_62_out, not_63_out, not_64_out, not_65_out, not_66_out,
       not_67_out, not_68_out, not_69_out, not_70_out, not_71_out, not_72_out, not_73_out, not_74_out,
       not_75_out, not_76_out, not_77_out, not_78_out, not_79_out, not_80_out, not_81_out, not_82_out,
       not_83_out, not_84_out, not_85_out, not_86_out, not_87_out, not_88_out, not_89_out, not_90_out,
       not_91_out, not_92_out, not_93_out, not_94_out, not_95_out, not_96_out, not_97_out, not_98_out,
       not_99_out, not_100_out, not_101_out, not_102_out, not_103_out, not_104_out, not_105_out, not_106_out,
       not_107_out, not_108_out, not_109_out, not_110_out, not_111_out, not_112_out, not_113_out,
       not_114_out, or_3_out, or_4_out;
  wire [7:0] and_6_out, and_7_out, and_8_out, and_9_out, bit_extender_1_out, bit_extender_2_out,
       bit_extender_3_out, bit_extender_4_out, or_2_out, ram_1_data, register_2_q, register_3_q, register_4_q;
  wire [15:0] bit_extender_10_out, multiplexer_2_out;
  wire [23:0] adder_1_out, adder_2_out, adder_3_out, adder_4_out, and_10_out, and_11_out, and_12_out,
       and_13_out, bit_extender_5_out, bit_extender_6_out, bit_extender_7_out, bit_extender_8_out,
       bit_extender_9_out, buffer_1_out, or_1_out;

  not not_1 (not_1_out, Clock);
  not not_2 (not_2_out, not_1_out);
  not not_3 (not_3_out, not_11_out);
  not not_4 (not_4_out, not_3_out);
  not not_5 (not_5_out, not_14_out);
  not not_6 (not_6_out, not_5_out);
  not not_7 (not_7_out, not_15_out);
  not not_8 (not_8_out, not_9_out);
  not not_9 (not_9_out, Clock);
  not not_10 (not_10_out, not_8_out);
  not not_11 (not_11_out, not_12_out);
  not not_12 (not_12_out, not_2_out);
  not not_13 (not_13_out, not_4_out);
  not not_14 (not_14_out, not_13_out);
  not not_15 (not_15_out, not_16_out);
  not not_16 (not_16_out, not_6_out);
  and and_1 (and_1_out, Width[0], Width[1]);
  not not_17 (not_17_out, not_19_out);
  not not_18 (not_18_out, not_10_out);
  not not_19 (not_19_out, not_18_out);
  and and_2 (and_2_out, Clock, not_1_out);
  and and_3 (and_3_out, not_11_out, ~and_1_out, not_3_out);  // AND_Gate
  and and_4 (and_4_out, not_14_out, ~Width[1], not_5_out);  // AND_Gate
  and and_5 (and_5_out, not_15_out, ~Width[1], not_7_out);  // AND_Gate
  not not_20 (not_20_out, not_17_out);
  not not_21 (not_21_out, not_20_out);
  Adder #(.width(24)) adder_1 (.a(Address[23:0]), .b({24{1'b0}}), .out(adder_1_out));  // open: cin, cout
  Adder #(.width(24)) adder_2 (.a(Address[23:0]), .b(24'h1), .out(adder_2_out));  // open: cin, cout
  Adder #(.width(24)) adder_3 (.a(Address[23:0]), .b(24'h2), .out(adder_3_out));  // open: cin, cout
  Adder #(.width(24)) adder_4 (.a(Address[23:0]), .b(24'h3), .out(adder_4_out));  // open: cin, cout
  assign bit_extender_1_out = {{7{and_2_out}}, and_2_out};  // Bit_Extender bit_extender_1
  assign bit_extender_2_out = {{7{and_3_out}}, and_3_out};  // Bit_Extender bit_extender_2
  assign bit_extender_3_out = {{7{and_4_out}}, and_4_out};  // Bit_Extender bit_extender_3
  assign bit_extender_4_out = {{7{and_5_out}}, and_5_out};  // Bit_Extender bit_extender_4
  not not_22 (not_22_out, not_24_out);
  not not_23 (not_23_out, not_22_out);
  not not_24 (not_24_out, not_21_out);
  assign bit_extender_5_out = {{23{and_2_out}}, and_2_out};  // Bit_Extender bit_extender_5
  assign bit_extender_6_out = {{23{and_3_out}}, and_3_out};  // Bit_Extender bit_extender_6
  assign bit_extender_7_out = {{23{and_4_out}}, and_4_out};  // Bit_Extender bit_extender_7
  assign bit_extender_8_out = {{23{and_5_out}}, and_5_out};  // Bit_Extender bit_extender_8
  assign and_6_out = bit_extender_1_out & Input[7:0];  // AND_Gate and_6, 8 bits wide
  assign and_7_out = bit_extender_2_out & Input[15:8];  // AND_Gate and_7, 8 bits wide
  assign and_8_out = bit_extender_3_out & Input[23:16];  // AND_Gate and_8, 8 bits wide
  assign and_9_out = bit_extender_4_out & Input[31:24];  // AND_Gate and_9, 8 bits wide
  not not_25 (not_25_out, not_26_out);
  not not_26 (not_26_out, not_23_out);
  not not_27 (not_27_out, not_25_out);
  assign and_10_out = bit_extender_5_out & adder_1_out;  // AND_Gate and_10, 24 bits wide
  assign and_11_out = bit_extender_6_out & adder_2_out;  // AND_Gate and_11, 24 bits wide
  assign and_12_out = bit_extender_7_out & adder_3_out;  // AND_Gate and_12, 24 bits wide
  assign and_13_out = bit_extender_8_out & adder_4_out;  // AND_Gate and_13, 24 bits wide
  not not_28 (not_28_out, not_29_out);
  not not_29 (not_29_out, not_27_out);
  assign or_1_out = and_10_out | and_11_out | and_12_out | and_13_out;  // OR_Gate or_1, 24 bits wide
  assign or_2_out = and_6_out | and_7_out | and_8_out | and_9_out;  // OR_Gate or_2, 8 bits wide
  not not_30 (not_30_out, and_2_out);
  not not_31 (not_31_out, not_30_out);
  not not_32 (not_32_out, not_31_out);
  not not_33 (not_33_out, not_32_out);
  not not_34 (not_34_out, not_33_out);
  not not_35 (not_35_out, not_34_out);
  not not_36 (not_36_out, not_35_out);
  not not_37 (not_37_out, and_3_out);
  not not_38 (not_38_out, not_37_out);
  not not_39 (not_39_out, not_38_out);
  not not_40 (not_40_out, not_39_out);
  not not_41 (not_41_out, not_40_out);
  not not_42 (not_42_out, not_41_out);
  not not_43 (not_43_out, not_42_out);
  not not_44 (not_44_out, and_4_out);
  not not_45 (not_45_out, not_44_out);
  not not_46 (not_46_out, not_45_out);
  not not_47 (not_47_out, not_46_out);
  not not_48 (not_48_out, not_47_out);
  not not_49 (not_49_out, not_48_out);
  not not_50 (not_50_out, not_49_out);
  not not_51 (not_51_out, and_5_out);
  not not_52 (not_52_out, not_51_out);
  not not_53 (not_53_out, not_52_out);
  not not_54 (not_54_out, not_53_out);
  not not_55 (not_55_out, not_54_out);
  not not_56 (not_56_out, not_55_out);
  not not_57 (not_57_out, not_56_out);
  not not_58 (not_58_out, not_59_out);
  not not_59 (not_59_out, not_60_out);
  not not_60 (not_60_out, not_28_out);
  assign buffer_1_out = or_1_out;  // Buffer buffer_1, 24 bits wide
  not not_61 (not_61_out, not_62_out);
  not not_62 (not_62_out, and_14_out);
  and and_14 (and_14_out, or_3_out, or_4_out);
  or or_3 (or_3_out, Load, Store);
  or or_4 (or_4_out, and_2_out, and_3_out, and_4_out, and_5_out);
  not not_63 (not_63_out, not_64_out);
  not not_64 (not_64_out, not_65_out);
  not not_65 (not_65_out, not_66_out);
  not not_66 (not_66_out, not_67_out);
  not not_67 (not_67_out, not_68_out);
  not not_68 (not_68_out, not_69_out);
  not not_69 (not_69_out, not_36_out);
  not not_70 (not_70_out, not_71_out);
  not not_71 (not_71_out, not_72_out);
  not not_72 (not_72_out, not_73_out);
  not not_73 (not_73_out, not_74_out);
  not not_74 (not_74_out, not_75_out);
  not not_75 (not_75_out, not_76_out);
  not not_76 (not_76_out, not_43_out);
  not not_77 (not_77_out, not_78_out);
  not not_78 (not_78_out, not_79_out);
  not not_79 (not_79_out, not_80_out);
  not not_80 (not_80_out, not_81_out);
  not not_81 (not_81_out, not_82_out);
  not not_82 (not_82_out, not_83_out);
  not not_83 (not_83_out, not_50_out);
  not not_84 (not_84_out, not_85_out);
  not not_85 (not_85_out, not_86_out);
  not not_86 (not_86_out, not_87_out);
  not not_87 (not_87_out, not_88_out);
  not not_88 (not_88_out, not_89_out);
  not not_89 (not_89_out, not_90_out);
  not not_90 (not_90_out, not_57_out);
  not not_91 (not_91_out, not_92_out);
  not not_92 (not_92_out, not_58_out);
  not not_93 (not_93_out, not_91_out);
  RAM #(.addrWidth(24), .bus("asynch")) ram_1 (
    .addr(buffer_1_out), .data(ram_1_data), .sel(not_61_out), .ld(Load), .clr(Clear));
  not not_94 (not_94_out, not_95_out);
  not not_95 (not_95_out, not_93_out);
  // Probe on or_1_out
  assign ram_1_data = Store ? or_2_out : 8'bz;  // Controlled_Buffer controlled_buffer_1
  // Probe on ram_1_data
  Register register_1 (.D(ram_1_data), .en(Load), .Q(Data[7:0]), .clk(not_63_out));  // open: clr
  Register register_2 (.D(ram_1_data), .en(Load), .Q(register_2_q), .clk(not_70_out), .clr(and_1_out));
  Register register_3 (.D(ram_1_data), .en(Load), .Q(register_3_q), .clk(not_77_out), .clr(Width[1]));
  Register register_4 (.D(ram_1_data), .en(Load), .Q(register_4_q), .clk(not_84_out), .clr(Width[1]));
  not not_96 (not_96_out, not_97_out);
  not not_97 (not_97_out, not_98_out);
  not not_98 (not_98_out, not_94_out);
  not not_99 (not_99_out, not_100_out);
  not not_100 (not_100_out, not_96_out);
  not not_101 (not_101_out, not_99_out);
  Multiplexer #(.width(24), .enable("false")) multiplexer_1 (
    .in0({multiplexer_2_out, register_2_q}), .in1(bit_extender_9_out), .out(Data[31:8]), .sel(and_15_out));
  assign bit_extender_9_out = {{23{Data[7]}}, Data[7]};  // Bit_Extender bit_extender_9
  and and_15 (and_15_out, and_1_out, Extend);
  Multiplexer #(.width(16), .enable("false")) multiplexer_2 (
    .in0({register_4_q, register_3_q}), .in1(bit_extender_10_out), .out(multiplexer_2_out), .sel(and_16_out));
  assign bit_extender_10_out = {{15{register_2_q[7]}}, register_2_q[7]};  // Bit_Extender bit_extender_10
  and and_16 (and_16_out, Width[1], Extend);
  not not_102 (not_102_out, not_103_out);
  not not_103 (not_103_out, not_101_out);
  not not_104 (not_104_out, not_105_out);
  not not_105 (not_105_out, not_106_out);
  not not_106 (not_106_out, not_102_out);
  not not_107 (not_107_out, not_104_out);
  not not_108 (not_108_out, not_109_out);
  not not_109 (not_109_out, not_107_out);
  not not_110 (not_110_out, not_108_out);
  not not_111 (not_111_out, not_110_out);
  not not_112 (not_112_out, not_114_out);
  not not_113 (not_113_out, not_111_out);
  not not_114 (not_114_out, not_113_out);
  not not_115 (DClock, not_112_out);
endmodule
