// Logisim project multiplexer.circ as structural Verilog
module main (
  input  [3:0] Selection,
  input  [3:0] in_2,
  input  [3:0] in_3,
  input  [3:0] in_4,
  input  [3:0] in_5,
  input  [3:0] in_6,
  input  [3:0] in_7,
  input  [3:0] in_8,
  input  [3:0] in_9,
  input  [3:0] in_10,
  input  [3:0] in_11,
  input  [3:0] in_12,
  input  [3:0] in_13,
  input  [3:0] in_14,
  input  [3:0] in_15,
  input  [3:0] in_16,
  input  [3:0] in_17,
  output [3:0] out_18
);

  wire and_1_out, and_2_out, and_3_out, and_4_out, and_5_out, and_6_out, and_7_out, and_8_out, and_9_out,
       and_10_out, and_11_out, and_12_out, and_13_out, and_14_out, and_15_out, and_16_out, and_17_out,
       and_18_out, and_19_out, and_20_out, and_21_out, and_22_out, and_23_out, and_24_out, and_25_out,
       and_26_out, and_27_out, and_28_out, and_29_out, and_30_out, and_31_out, and_32_out, and_33_out,
       and_34_out, and_35_out, and_36_out, and_37_out, and_38_out, and_39_out, and_40_out, and_41_out,
       and_42_out, and_43_out, and_44_out, and_45_out, and_46_out, and_47_out, and_48_out, and_49_out,
       and_50_out, and_51_out, and_52_out, and_53_out, and_54_out, and_55_out, and_56_out, and_57_out,
       and_58_out, and_59_out, and_60_out, and_61_out, and_62_out, and_63_out, and_64_out, and_65_out,
       and_66_out, and_67_out, and_68_out, and_69_out, and_70_out, and_71_out, and_72_out, and_73_out,
       and_74_out, and_75_out, and_76_out, and_77_out, and_78_out, and_79_out, and_80_out, not_1_out,
       not_2_out, not_3_out, not_4_out, or_3_out, or_4_out, or_5_out, or_6_out, or_7_out, or_8_out, or_9_out,
       or_10_out, or_11_out, or_12_out, or_13_out, or_14_out, or_15_out, or_16_out, or_17_out, or_18_out,
       or_19_out, or_20_out, or_21_out, or_22_out, or_23_out, or_24_out, or_25_out, or_26_out, or_27_out,
       or_28_out, or_29_out, or_30_out, or_31_out, or_32_out, or_35_out, or_36_out, or_37_out, or_38_out,
       or_39_out, or_40_out, or_41_out, or_42_out, or_43_out, or_44_out, or_45_out, or_46_out, or_47_out,
       or_48_out, or_49_out, or_50_out, or_51_out, or_52_out, or_53_out, or_54_out, or_55_out, or_56_out,
       or_57_out, or_58_out, or_59_out, or_60_out, or_61_out, or_62_out, or_63_out, or_64_out;

  not not_1 (not_1_out, Selection[3]);
  not not_2 (not_2_out, Selection[2]);
  not not_3 (not_3_out, Selection[0]);
  not not_4 (not_4_out, Selection[1]);
  and and_1 (and_1_out, not_3_out, not_4_out, not_2_out, not_1_out);
  and and_2 (and_2_out, Selection[0], not_4_out, not_2_out, not_1_out);
  and and_3 (and_3_out, not_3_out, Selection[1], not_2_out, not_1_out);
  and and_4 (and_4_out, Selection[0], Selection[1], not_2_out, not_1_out);
  and and_5 (and_5_out, not_3_out, not_4_out, Selection[2], not_1_out);
  and and_6 (and_6_out, Selection[0], not_4_out, Selection[2], not_1_out);
  and and_7 (and_7_out, not_3_out, Selection[1], Selection[2], not_1_out);
  and and_8 (and_8_out, Selection[0], Selection[1], Selection[2], not_1_out);
  and and_9 (and_9_out, not_3_out, not_4_out, not_2_out, Selection[3]);
  and and_10 (and_10_out, Selection[0], not_4_out, not_2_out, Selection[3]);
  and and_11 (and_11_out, not_3_out, Selection[1], not_2_out, Selection[3]);
  and and_12 (and_12_out, Selection[0], Selection[1], not_2_out, Selection[3]);
  and and_13 (and_13_out, not_3_out, not_4_out, Selection[2], Selection[3]);
  and and_14 (and_14_out, Selection[0], not_4_out, Selection[2], Selection[3]);
  and and_15 (and_15_out, not_3_out, Selection[1], Selection[2], Selection[3]);
  and and_16 (and_16_out, Selection[0], Selection[1], Selection[2], Selection[3]);
  or or_1 (out_18[3], or_3_out, and_65_out);
  or or_2 (out_18[2], or_4_out, and_49_out);
  or or_3 (or_3_out, or_6_out, and_66_out);
  or or_4 (or_4_out, or_5_out, and_50_out);
  or or_5 (or_5_out, or_8_out, and_51_out);
  or or_6 (or_6_out, or_7_out, and_67_out);
  or or_7 (or_7_out, or_10_out, and_68_out);
  or or_8 (or_8_out, or_9_out, and_52_out);
  or or_9 (or_9_out, or_11_out, and_53_out);
  or or_10 (or_10_out, or_12_out, and_69_out);
  or or_11 (or_11_out, or_13_out, and_54_out);
  or or_12 (or_12_out, or_14_out, and_70_out);
  or or_13 (or_13_out, or_16_out, and_55_out);
  or or_14 (or_14_out, or_15_out, and_71_out);
  or or_15 (or_15_out, or_17_out, and_72_out);
  or or_16 (or_16_out, or_18_out, and_56_out);
  or or_17 (or_17_out, or_19_out, and_73_out);
  or or_18 (or_18_out, or_20_out, and_57_out);
  or or_19 (or_19_out, or_21_out, and_74_out);
  or or_20 (or_20_out, or_22_out, and_58_out);
  or or_21 (or_21_out, or_23_out, and_75_out);
  or or_22 (or_22_out, or_24_out, and_59_out);
  or or_23 (or_23_out, or_25_out, and_76_out);
  or or_24 (or_24_out, or_26_out, and_60_out);
  or or_25 (or_25_out, or_28_out, and_77_out);
  or or_26 (or_26_out, or_27_out, and_61_out);
  or or_27 (or_27_out, or_30_out, and_62_out);
  or or_28 (or_28_out, or_29_out, and_78_out);
  or or_29 (or_29_out, or_31_out, and_79_out);
  or or_30 (or_30_out, or_32_out, and_63_out);
  buf or_31 (or_31_out, and_80_out);  // OR_Gate
  buf or_32 (or_32_out, and_64_out);  // OR_Gate
  or or_33 (out_18[0], or_36_out, and_17_out);
  or or_34 (out_18[1], or_35_out, and_18_out);
  or or_35 (or_35_out, or_38_out, and_20_out);
  or or_36 (or_36_out, or_37_out, and_19_out);
  or or_37 (or_37_out, or_40_out, and_21_out);
  or or_38 (or_38_out, or_39_out, and_22_out);
  or or_39 (or_39_out, or_42_out, and_24_out);
  or or_40 (or_40_out, or_41_out, and_23_out);
  or or_41 (or_41_out, or_44_out, and_25_out);
  or or_42 (or_42_out, or_43_out, and_26_out);
  or or_43 (or_43_out, or_45_out, and_28_out);
  or or_44 (or_44_out, or_46_out, and_27_out);
  or or_45 (or_45_out, or_48_out, and_30_out);
  or or_46 (or_46_out, or_47_out, and_29_out);
  or or_47 (or_47_out, or_50_out, and_31_out);
  or or_48 (or_48_out, or_49_out, and_32_out);
  or or_49 (or_49_out, or_51_out, and_34_out);
  or or_50 (or_50_out, or_52_out, and_33_out);
  or or_51 (or_51_out, or_54_out, and_36_out);
  or or_52 (or_52_out, or_53_out, and_35_out);
  or or_53 (or_53_out, or_56_out, and_37_out);
  or or_54 (or_54_out, or_55_out, and_38_out);
  or or_55 (or_55_out, or_58_out, and_40_out);
  or or_56 (or_56_out, or_57_out, and_39_out);
  or or_57 (or_57_out, or_59_out, and_41_out);
  or or_58 (or_58_out, or_60_out, and_42_out);
  or or_59 (or_59_out, or_61_out, and_43_out);
  or or_60 (or_60_out, or_62_out, and_44_out);
  or or_61 (or_61_out, or_64_out, and_45_out);
  or or_62 (or_62_out, or_63_out, and_46_out);
  buf or_63 (or_63_out, and_48_out);  // OR_Gate
  buf or_64 (or_64_out, and_47_out);  // OR_Gate
  and and_17 (and_17_out, in_2[0], and_1_out);
  and and_18 (and_18_out, in_2[1], and_1_out);
  and and_19 (and_19_out, in_3[0], and_2_out);
  and and_20 (and_20_out, in_3[1], and_2_out);
  and and_21 (and_21_out, in_4[0], and_3_out);
  and and_22 (and_22_out, in_4[1], and_3_out);
  and and_23 (and_23_out, in_5[0], and_4_out);
  and and_24 (and_24_out, in_5[1], and_4_out);
  and and_25 (and_25_out, in_6[0], and_5_out);
  and and_26 (and_26_out, in_6[1], and_5_out);
  and and_27 (and_27_out, in_7[0], and_6_out);
  and and_28 (and_28_out, in_7[1], and_6_out);
  and and_29 (and_29_out, in_8[0], and_7_out);
  and and_30 (and_30_out, in_8[1], and_7_out);
  and and_31 (and_31_out, in_9[0], and_8_out);
  and and_32 (and_32_out, in_9[1], and_8_out);
  and and_33 (and_33_out, in_10[0], and_9_out);
  and and_34 (and_34_out, in_10[1], and_9_out);
  and and_35 (and_35_out, in_11[0], and_10_out);
  and and_36 (and_36_out, in_11[1], and_10_out);
  and and_37 (and_37_out, in_12[0], and_11_out);
  and and_38 (and_38_out, in_12[1], and_11_out);
  and and_39 (and_39_out, in_13[0], and_12_out);
  and and_40 (and_40_out, in_13[1], and_12_out);
  and and_41 (and_41_out, in_14[0], and_13_out);
  and and_42 (and_42_out, in_14[1], and_13_out);
  and and_43 (and_43_out, in_15[0], and_14_out);
  and and_44 (and_44_out, in_15[1], and_14_out);
  and and_45 (and_45_out, in_16[0], and_15_out);
  and and_46 (and_46_out, in_16[1], and_15_out);
  and and_47 (and_47_out, in_17[0], and_16_out);
  and and_48 (and_48_out, in_17[1], and_16_out);
  and and_49 (and_49_out, in_2[2], and_1_out);
  and and_50 (and_50_out, in_3[2], and_2_out);
  and and_51 (and_51_out, in_4[2], and_3_out);
  and and_52 (and_52_out, in_5[2], and_4_out);
  and and_53 (and_53_out, in_6[2], and_5_out);
  and and_54 (and_54_out, in_7[2], and_6_out);
  and and_55 (and_55_out, in_8[2], and_7_out);
  and and_56 (and_56_out, in_9[2], and_8_out);
  and and_57 (and_57_out, in_10[2], and_9_out);
  and and_58 (and_58_out, in_11[2], and_10_out);
  and and_59 (and_59_out, in_12[2], and_11_out);
  and and_60 (and_60_out, in_13[2], and_12_out);
  and and_61 (and_61_out, in_14[2], and_13_out);
  and and_62 (and_62_out, in_15[2], and_14_out);
  and and_63 (and_63_out, in_16[2], and_15_out);
  and and_64 (and_64_out, in_17[2], and_16_out);
  and and_65 (and_65_out, in_2[3], and_1_out);
  and and_66 (and_66_out, in_3[3], and_2_out);
  and and_67 (and_67_out, in_4[3], and_3_out);
  and and_68 (and_68_out, in_5[3], and_4_out);
  and and_69 (and_69_out, in_6[3], and_5_out);
  and and_70 (and_70_out, in_7[3], and_6_out);
  and and_71 (and_71_out, in_8[3], and_7_out);
  and and_72 (and_72_out, in_9[3], and_8_out);
  and and_73 (and_73_out, in_10[3], and_9_out);
  and and_74 (and_74_out, in_11[3], and_10_out);
  and and_75 (and_75_out, in_12[3], and_11_out);
  and and_76 (and_76_out, in_13[3], and_12_out);
  and and_77 (and_77_out, in_14[3], and_13_out);
  and and_78 (and_78_out, in_15[3], and_14_out);
  and and_79 (and_79_out, in_16[3], and_15_out);
  and and_80 (and_80_out, in_17[3], and_16_out);
endmodule
