// Logisim project regfile.circ as structural Verilog: 1 circuit, main circuit main
module main (
  input  [11:0] in_1
);

  wire decoder_2_out0, decoder_2_out1, decoder_2_out2, decoder_2_out3, decoder_2_out4, decoder_2_out5,
       decoder_2_out6, decoder_2_out7, decoder_3_out0, decoder_3_out1, decoder_3_out2, decoder_3_out3,
       decoder_3_out4, decoder_3_out5, decoder_3_out6, decoder_3_out7, decoder_4_out0, decoder_4_out1,
       decoder_4_out2, decoder_4_out3, decoder_4_out4, decoder_4_out5, decoder_4_out6, decoder_4_out7,
       decoder_5_out0, decoder_5_out1, decoder_5_out2, decoder_5_out3, decoder_5_out4, decoder_5_out5,
       decoder_5_out6, decoder_5_out7, undriven_3, undriven_4, undriven_9, undriven_11, undriven_14,
       undriven_15, undriven_18, undriven_19;
  wire [2:0] undriven, undriven_6, undriven_7, undriven_10, undriven_12, undriven_16;
  wire [5:0] undriven_5;
  wire [31:0] M00, M01, M02, M03, M10, M11, M12, M13, register_1_q, register_2_q, register_3_q, register_4_q,
       register_5_q, register_6_q, register_7_q, register_8_q, register_9_q, register_10_q, register_11_q,
       register_12_q, register_13_q, register_14_q, register_15_q, register_16_q, register_17_q,
       register_18_q, register_19_q, register_20_q, register_21_q, register_22_q, register_23_q,
       register_24_q, register_25_q, register_26_q, register_27_q, register_28_q, register_29_q,
       register_30_q, register_31_q, register_32_q, undriven_2, undriven_8, undriven_13, undriven_17;

  Decoder decoder_1 ();  // open: out0, out1, sel, en
  Decoder #(.select(3), .disabled(0)) decoder_2 (
    .out0(decoder_2_out0), .out1(decoder_2_out1), .out2(decoder_2_out2), .out3(decoder_2_out3),
    .out4(decoder_2_out4), .out5(decoder_2_out5), .out6(decoder_2_out6), .out7(decoder_2_out7),
    .sel(undriven), .en(undriven_3));
  Register #(.width(32)) register_1 (
    .D(undriven_2), .en(decoder_2_out0), .Q(register_1_q), .clk(undriven_4), .clr(1'b1));
  Register #(.width(32)) register_2 (
    .D(undriven_2), .en(decoder_2_out1), .Q(register_2_q), .clk(undriven_4));  // open: clr
  Register #(.width(32)) register_3 (
    .D(undriven_2), .en(decoder_2_out2), .Q(register_3_q), .clk(undriven_4));  // open: clr
  Register #(.width(32)) register_4 (
    .D(undriven_2), .en(decoder_2_out3), .Q(register_4_q), .clk(undriven_4));  // open: clr
  Register #(.width(32)) register_5 (
    .D(undriven_2), .en(decoder_2_out4), .Q(register_5_q), .clk(undriven_4));  // open: clr
  Register #(.width(32)) register_6 (
    .D(undriven_2), .en(decoder_2_out5), .Q(register_6_q), .clk(undriven_4));  // open: clr
  Register #(.width(32)) register_7 (
    .D(undriven_2), .en(decoder_2_out6), .Q(register_7_q), .clk(undriven_4));  // open: clr
  Register #(.width(32)) register_8 (
    .D(undriven_2), .en(decoder_2_out7), .Q(register_8_q), .clk(undriven_4));  // open: clr
  Multiplexer #(.select(3), .width(32), .enable("false")) multiplexer_1 (
    .in0(register_1_q), .in1(register_2_q), .in2(register_3_q), .in3(register_4_q), .in4(register_5_q),
    .in5(register_6_q), .in6(register_7_q), .in7(register_8_q), .out(M00), .sel(in_1[2:0]));
  Multiplexer #(.select(3), .width(32), .enable("false")) multiplexer_2 (
    .in0(register_1_q), .in1(register_2_q), .in2(register_3_q), .in3(register_4_q), .in4(register_5_q),
    .in5(register_6_q), .in6(register_7_q), .in7(register_8_q), .out(M10), .sel(undriven_5[2:0]));
  Decoder #(.select(3), .disabled(0)) decoder_3 (
    .out0(decoder_3_out0), .out1(decoder_3_out1), .out2(decoder_3_out2), .out3(decoder_3_out3),
    .out4(decoder_3_out4), .out5(decoder_3_out5), .out6(decoder_3_out6), .out7(decoder_3_out7),
    .sel(undriven_10), .en(undriven_9));
  Register #(.width(32)) register_9 (
    .D(undriven_8), .en(decoder_3_out0), .Q(register_9_q), .clk(undriven_11), .clr(1'b1));
  Register #(.width(32)) register_10 (
    .D(undriven_8), .en(decoder_3_out1), .Q(register_10_q), .clk(undriven_11));  // open: clr
  Register #(.width(32)) register_11 (
    .D(undriven_8), .en(decoder_3_out2), .Q(register_11_q), .clk(undriven_11));  // open: clr
  Register #(.width(32)) register_12 (
    .D(undriven_8), .en(decoder_3_out3), .Q(register_12_q), .clk(undriven_11));  // open: clr
  Register #(.width(32)) register_13 (
    .D(undriven_8), .en(decoder_3_out4), .Q(register_13_q), .clk(undriven_11));  // open: clr
  Register #(.width(32)) register_14 (
    .D(undriven_8), .en(decoder_3_out5), .Q(register_14_q), .clk(undriven_11));  // open: clr
  Register #(.width(32)) register_15 (
    .D(undriven_8), .en(decoder_3_out6), .Q(register_15_q), .clk(undriven_11));  // open: clr
  Register #(.width(32)) register_16 (
    .D(undriven_8), .en(decoder_3_out7), .Q(register_16_q), .clk(undriven_11));  // open: clr
  Multiplexer #(.select(3), .width(32), .enable("false")) multiplexer_3 (
    .in0(register_9_q), .in1(register_10_q), .in2(register_11_q), .in3(register_12_q), .in4(register_13_q),
    .in5(register_14_q), .in6(register_15_q), .in7(register_16_q), .out(M01), .sel(in_1[5:3]));
  Multiplexer #(.select(3), .width(32), .enable("false")) multiplexer_4 (
    .in0(register_9_q), .in1(register_10_q), .in2(register_11_q), .in3(register_12_q), .in4(register_13_q),
    .in5(register_14_q), .in6(register_15_q), .in7(register_16_q), .out(M11), .sel(undriven_5[5:3]));
  Decoder #(.select(3), .disabled(0)) decoder_4 (
    .out0(decoder_4_out0), .out1(decoder_4_out1), .out2(decoder_4_out2), .out3(decoder_4_out3),
    .out4(decoder_4_out4), .out5(decoder_4_out5), .out6(decoder_4_out6), .out7(decoder_4_out7),
    .sel(undriven_12), .en(undriven_14));
  Register #(.width(32)) register_17 (
    .D(undriven_13), .en(decoder_4_out0), .Q(register_17_q), .clk(undriven_15));  // open: clr
  Register #(.width(32)) register_18 (
    .D(undriven_13), .en(decoder_4_out1), .Q(register_18_q), .clk(undriven_15));  // open: clr
  Register #(.width(32)) register_19 (
    .D(undriven_13), .en(decoder_4_out2), .Q(register_19_q), .clk(undriven_15));  // open: clr
  Register #(.width(32)) register_20 (
    .D(undriven_13), .en(decoder_4_out3), .Q(register_20_q), .clk(undriven_15));  // open: clr
  Register #(.width(32)) register_21 (
    .D(undriven_13), .en(decoder_4_out4), .Q(register_21_q), .clk(undriven_15));  // open: clr
  Register #(.width(32)) register_22 (
    .D(undriven_13), .en(decoder_4_out5), .Q(register_22_q), .clk(undriven_15));  // open: clr
  Register #(.width(32)) register_23 (
    .D(undriven_13), .en(decoder_4_out6), .Q(register_23_q), .clk(undriven_15));  // open: clr
  Register #(.width(32)) register_24 (
    .D(undriven_13), .en(decoder_4_out7), .Q(register_24_q), .clk(undriven_15));  // open: clr
  Multiplexer #(.select(3), .width(32), .enable("false")) multiplexer_5 (
    .in0(register_17_q), .in1(register_18_q), .in2(register_19_q), .in3(register_20_q), .in4(register_21_q),
    .in5(register_22_q), .in6(register_23_q), .in7(register_24_q), .out(M02), .sel(in_1[8:6]));
  Multiplexer #(.select(3), .width(32), .enable("false")) multiplexer_6 (
    .in0(register_17_q), .in1(register_18_q), .in2(register_19_q), .in3(register_20_q), .in4(register_21_q),
    .in5(register_22_q), .in6(register_23_q), .in7(register_24_q), .out(M12), .sel(undriven_6));
  Decoder #(.select(3), .disabled(0)) decoder_5 (
    .out0(decoder_5_out0), .out1(decoder_5_out1), .out2(decoder_5_out2), .out3(decoder_5_out3),
    .out4(decoder_5_out4), .out5(decoder_5_out5), .out6(decoder_5_out6), .out7(decoder_5_out7),
    .sel(undriven_16), .en(undriven_18));
  Register #(.width(32)) register_25 (
    .D(undriven_17), .en(decoder_5_out0), .Q(register_25_q), .clk(undriven_19));  // open: clr
  Register #(.width(32)) register_26 (
    .D(undriven_17), .en(decoder_5_out1), .Q(register_26_q), .clk(undriven_19));  // open: clr
  Register #(.width(32)) register_27 (
    .D(undriven_17), .en(decoder_5_out2), .Q(register_27_q), .clk(undriven_19));  // open: clr
  Register #(.width(32)) register_28 (
    .D(undriven_17), .en(decoder_5_out3), .Q(register_28_q), .clk(undriven_19));  // open: clr
  Register #(.width(32)) register_29 (
    .D(undriven_17), .en(decoder_5_out4), .Q(register_29_q), .clk(undriven_19));  // open: clr
  Register #(.width(32)) register_30 (
    .D(undriven_17), .en(decoder_5_out5), .Q(register_30_q), .clk(undriven_19));  // open: clr
  Register #(.width(32)) register_31 (
    .D(undriven_17), .en(decoder_5_out6), .Q(register_31_q), .clk(undriven_19));  // open: clr
  Register #(.width(32)) register_32 (
    .D(undriven_17), .en(decoder_5_out7), .Q(register_32_q), .clk(undriven_19));  // open: clr
  Multiplexer #(.select(3), .width(32), .enable("false")) multiplexer_7 (
    .in0(register_25_q), .in1(register_26_q), .in2(register_27_q), .in3(register_28_q), .in4(register_29_q),
    .in5(register_30_q), .in6(register_31_q), .in7(register_32_q), .out(M03), .sel(in_1[11:9]));
  Multiplexer #(.select(3), .width(32), .enable("false")) multiplexer_8 (
    .in0(register_25_q), .in1(register_26_q), .in2(register_27_q), .in3(register_28_q), .in4(register_29_q),
    .in5(register_30_q), .in6(register_31_q), .in7(register_32_q), .out(M13), .sel(undriven_7));
  Multiplexer #(.select(2), .width(32), .enable("false")) multiplexer_9 ();  // open: in0, in1, in2, in3, out, sel
  Multiplexer #(.select(2), .width(32), .enable("false")) multiplexer_10 ();  // open: in0, in1, in2, in3, out, sel
endmodule
